# Fritzing sketch WeMos_LEDstrip_Nextion_DHT (saved by Fritzing 0.9.3b)
circuit board: 7.33844cm x 7.37353cm
breadboards: 1

parts:
  R4 = Resistor [tolerance=±5% resistance=470 package=THT]
  IC1 = IC, DIP package, 20 pins [chip_label="SN74HCT245N " part_number=SN74HCT245N]
  C1 = Electrolytic Capacitor [capacitance=1µF package="100 mil [THT, electrolytic]"]
  F1 = FUSE [package=fuse_5mm]
  J1 = Screw terminal - 2 pins [package=THT]
  J2 = screw terminal, 3 pins
  WeMos_D1_Mini1 = WeMos D1 Mini
  DS1 = DS18B20 1-Wire Temperature Sensor [part_number=DS18B20]
  R5 = Resistor [tolerance=±5% resistance=4.7k package=THT]
  J3 = screw terminal, 3 pins
  R3 = Resistor [tolerance=±5% resistance=470 package=THT]
  J4 = screw terminal, 3 pins
  J5 = screw terminal, 3 pins
  R2 = Resistor [tolerance=±5% resistance=470 package=THT]
  R1 = Resistor [tolerance=±5% resistance=470 package=THT]
  J6 = female pin header, 8 pins [form="♀ (female)"]
  R6 = Bussed6 Resistor-6 (SIP-7) [tolerance=±5% resistance=10000 package=SIP-7]
  J7 = female pin header, 7 pins [form="♀ (female)"]
  J8 = female pin header, 9 pins [form="♀ (female)"]
  J9 = female pin header, 4 pins [form="♀ (female)"]
  R9 = Resistor [tolerance=±5% resistance=1k package=THT]
  R7 = Resistor [tolerance=±5% resistance=1k package=THT]
  R8 = Resistor [tolerance=±5% resistance=1k package=THT]
  R10 = Resistor [tolerance=±5% resistance=1k package=THT]
  R11 = Resistor [tolerance=±5% resistance=1k package=THT]
  R12 = Resistor [tolerance=±5% resistance=1k package=THT]

nets:
  N1: R4.Pin_0, J2.pin2
  N2: R4.Pin_1, IC1.pin3
  N3: IC1.pin1, IC1.pin10, IC1.pin19, C1.-, J1.pin1, J2.pin1, WeMos_D1_Mini1.G, DS1.GND, J3.pin1, J4.pin1, J5.pin1, J6.pin7, R6.Pin_0, J8.pin2, J8.pin3, J8.pin4, J8.pin5, J8.pin6, J8.pin7, J8.pin8, J9.pin4
  N4: IC1.pin4, R3.Pin_1
  N5: IC1.pin5, R2.Pin_1
  N6: IC1.pin6, R1.Pin_1
  N7: IC1.pin14, WeMos_D1_Mini1.D7
  N8: IC1.pin15, WeMos_D1_Mini1.D4
  N9: IC1.pin16, WeMos_D1_Mini1.TX
  N10: IC1.pin17, WeMos_D1_Mini1.RX
  N11: IC1.pin20, C1.+, F1.2, J2.pin3, WeMos_D1_Mini1.5V, J3.pin3, J4.pin3, J5.pin3, J8.pin1, J9.pin1
  N12: F1.1, J1.pin2
  3V3: WeMos_D1_Mini1.3V3, DS1.VDD, R5.Pin_1, J7.pin1, J7.pin2, J7.pin3, J7.pin4, J7.pin5, J7.pin6, J7.pin7
  N13: WeMos_D1_Mini1.A0, J6.pin8
  N14: WeMos_D1_Mini1.D0, R12.Pin_1
  N15: WeMos_D1_Mini1.D1, R8.Pin_1
  N16: WeMos_D1_Mini1.D2, R7.Pin_1
  N17: WeMos_D1_Mini1.D3, DS1.DQ, R5.Pin_0
  N18: WeMos_D1_Mini1.D5, J9.pin3, R11.Pin_1
  N19: WeMos_D1_Mini1.D6, J9.pin2, R10.Pin_1
  N20: WeMos_D1_Mini1.D8, R9.Pin_1
  N21: WeMos_D1_Mini1.RST, J8.pin9
  N22: J3.pin2, R3.Pin_0
  N23: J4.pin2, R2.Pin_0
  N24: J5.pin2, R1.Pin_0
  N25: J6.pin1, R6.Pin_6, R7.Pin_0
  N26: J6.pin2, R6.Pin_5, R8.Pin_0
  N27: J6.pin3, R6.Pin_4, R9.Pin_0
  N28: J6.pin4, R6.Pin_3, R10.Pin_0
  N29: J6.pin5, R6.Pin_2, R11.Pin_0
  N30: J6.pin6, R6.Pin_1, R12.Pin_0

notes:
  3V3 D2 D1 D8 D6 D5 D0 GND A0
  5V |->       GND      <-| RST
  3V3 ->
  GND  D  5V
  GND 5V
  GND D5 D6 5V
  D7 D4 TX
  RX
  SuperLEDstrip
  Rev 1.1 (22.06.2018)

custom parts:
  Bussed6 Resistor-6 (SIP-7): A resistor array is a single package which contains more than one resistor. They are typically used for convenience when several resistors are needed together in the same place in a circuit.
