# Fritzing sketch WeMos_LEDstrip_Nextion_DHT_LED (saved by Fritzing 0.9.3b)
breadboards: 1
perfboards: 1

parts:
  NEOPIXEL1 = Neopixel Strip -- Black (30/m)
  R1 = Resistor [tolerance=±5% resistance=470 package=THT]
  IC1 = IC, DIP package, 20 pins [chip_label="SN74HCT245N " part_number=SN74HCT245N]
  Power_plug1 = Power plug
  C1 = Electrolytic Capacitor [capacitance=1µF package="100 mil [THT, electrolytic]"]
  DHT1 = DHT22 Humidity and Temperature Sensor
  R2 = Resistor [tolerance=±5% resistance=220 package="2512 [SMD]"]
  WeMos_D1_Mini1 = WeMos D1 Mini
  LED1 = LEDs [package=led10mm]

nets:
  GND: NEOPIXEL1.GND, IC1.pin1, IC1.pin10, IC1.pin19, Power_plug1.GND, C1.-, DHT1.GND, WeMos_D1_Mini1.G, LED1.A
  N1: NEOPIXEL1.Din, R1.Pin_0
  +5V: NEOPIXEL1.+5V, IC1.pin20, Power_plug1.VCC, C1.+, R2.Pin_1, WeMos_D1_Mini1.5V
  N2: R1.Pin_1, IC1.pin3
  N3: IC1.pin17, WeMos_D1_Mini1.D3
  N4: DHT1.VDD, WeMos_D1_Mini1.D0
  N5: DHT1.DATA, WeMos_D1_Mini1.D4

custom parts:
  Neopixel Strip -- Black (30/m): These NeoPixel strips have 30 digitally-addressable pixel LEDs per meter and are very affordable and are only 12.5 mm wide, 10 mm if you remove the strip from the casing.
