# Fritzing sketch WeMos_LEDstrip_Nextion_DHT_LED_printed-circuit-board (saved by Fritzing 0.9.3b)
circuit board: 7.15629cm x 9.29727cm
breadboards: 1

parts:
  R1 = Resistor [tolerance=±5% resistance=470 package=THT]
  IC1 = IC, DIP package, 20 pins [chip_label="SN74HCT245N " part_number=SN74HCT245N]
  C1 = Electrolytic Capacitor [capacitance=1µF voltage=16V package="100 mil [THT, electrolytic]"]
  DHT1 = DHT22 Humidity and Temperature Sensor
  Display = Header 4 [package=molex-1x4_lock]
  LED2 = LED - 5mm [color="Green (555nm)" package="5 mm [THT]"]
  F1 = FUSE [package=fuse_5mm]
  R3 = Resistor [tolerance=±5% resistance=470 package=THT]
  Power_In = Screw terminal - 2 pins [package=THT]
  terminal_for_LED = screw terminal, 3 pins
  WeMos_D1_Mini1 = WeMos D1 Mini

nets:
  N1: R1.Pin_0, terminal_for_LED.pin2
  N2: R1.Pin_1, IC1.pin3
  N3: IC1.pin1, IC1.pin10, IC1.pin19, C1.-, DHT1.GND, Display.4, LED2.cathode, Power_In.pin1, terminal_for_LED.pin1
  N4: IC1.pin20, C1.+, Display.1, F1.2, R3.Pin_1, terminal_for_LED.pin3
  N5: DHT1.VDD, WeMos_D1_Mini1.D0
  N6: DHT1.DATA, WeMos_D1_Mini1.D4
  N7: LED2.anode, R3.Pin_0
  N8: F1.1, Power_In.pin2
